// Logisim project lec02-sample.circ as structural Verilog: 1 circuit, main circuit main
module main (
  input  in_1,
  input  in_2
);

  wire and_1_out, buffer_1_out, not_1_out, or_1_out, xor_1_out;

  not not_1 (not_1_out, in_1);
  buf buffer_1 (buffer_1_out, in_2);
  buf and_1 (and_1_out, not_1_out);  // AND_Gate
  or or_1 (or_1_out, not_1_out, buffer_1_out);
  xor xor_1 (xor_1_out, and_1_out, or_1_out);
  LED led_1 (.in(xor_1_out));
endmodule
