// Logisim project lec02-alu.circ as structural Verilog: 1 circuit, main circuit main
module main (
  input  B0,
  input  B1,
  input  A0,
  input  A1,
  input  t0,
  input  t1
);

  wire and_1_out, and_2_out, and_3_out, and_4_out, and_5_out, and_6_out, and_7_out, and_8_out, and_9_out,
       and_10_out, and_11_out, and_12_out, and_14_out, and_15_out, and_16_out, and_17_out, not_1_out,
       not_2_out, not_3_out, not_4_out, not_5_out, not_6_out, or_1_out, or_2_out, or_3_out, or_4_out,
       or_5_out, xor_1_out, xor_2_out, xor_3_out;

  not not_1 (not_1_out, t0);
  not not_2 (not_2_out, t1);
  not not_3 (not_3_out, t1);
  not not_4 (not_4_out, t0);
  and and_1 (and_1_out, t1, t0);
  and and_2 (and_2_out, t1, not_1_out);
  and and_3 (and_3_out, not_2_out, t0);
  and and_4 (and_4_out, not_3_out, not_4_out);
  and and_5 (and_5_out, B0, A0);
  and and_6 (and_6_out, and_5_out, and_1_out);
  not not_5 (not_5_out, A0);
  and and_7 (and_7_out, not_5_out, and_2_out);
  or or_1 (or_1_out, and_6_out, and_7_out, and_8_out, and_9_out);
  or or_2 (or_2_out, B0, A0);
  and and_8 (and_8_out, or_2_out, and_3_out);
  xor xor_1 (xor_1_out, B0, A0);
  and and_9 (and_9_out, xor_1_out, and_4_out);
  and and_10 (and_10_out, and_4_out, A0, B0);
  and and_11 (and_11_out, B1, A1);
  and and_12 (and_12_out, and_11_out, and_1_out);
  LED led_1 (.in(or_4_out));
  LED led_2 (.in(or_1_out));
  not not_6 (not_6_out, A1);
  // AND_Gate and_13 has open pins: in1=not_6_out, in3=and_2_out, out=open
  or or_3 (or_3_out, B1, A1);
  and and_14 (and_14_out, or_3_out, and_3_out);
  xor xor_2 (xor_2_out, and_10_out, xor_3_out);
  or or_4 (or_4_out, and_12_out, and_14_out, and_15_out);
  xor xor_3 (xor_3_out, B1, A1);
  and and_15 (and_15_out, xor_2_out, and_4_out);
  and and_16 (and_16_out, and_4_out, B1, A1);
  and and_17 (and_17_out, and_4_out, xor_3_out, and_10_out);
  or or_5 (or_5_out, and_16_out, and_17_out);
  LED led_3 (.in(or_5_out));

  // Notes on the sheet:
  //   C0
  //   C1
  //   Overflow
endmodule
