// Logisim project lec02-sample-3.circ as structural Verilog: 1 circuit, main circuit main
module main (
  input  A,
  input  B,
  input  C
);

  wire and_1_out, and_2_out, nor_1_out, not_1_out, or_1_out;

  or or_1 (or_1_out, A, B);
  nor nor_1 (nor_1_out, B, C);
  not not_1 (not_1_out, A);
  LED led_1 (.in(nor_1_out));
  and and_1 (and_1_out, not_1_out, or_1_out);
  and and_2 (and_2_out, and_1_out, nor_1_out);
  LED led_2 (.in(and_2_out));

  // Notes on the sheet:
  //   B XOR C
  //   (not A) (A + B) = 0 if B = 0
endmodule
